# Fritzing sketch adafruit.circuit.playground.express (saved by Fritzing 0.9.3b)

parts:
  BUTTON1 = Arcade Button (red)
  BUTTON2 = Arcade Button (green)
  LED1 = LED - 3mm [color="Red (633nm)" package="3 mm [THT]"]
  LED2 = LED - 3mm [color="Red (633nm)" package="3 mm [THT]"]
  Part1 = Adafruit Micro USB Breakout [part_number="Adafruit #1833"]
  Adafruit_Circuit_Playground_Express = Adafruit Circuit Playground Dev Edition
  WS2812_LED_STRIP = Neopixel Strip -- Black (60/m)
  U1 = SWITCH_SPDT [package=kps-1290]
  R1 = Resistor [tolerance=±5% resistance=10k package=THT]
  R2 = Resistor [tolerance=±5% resistance=10k package=THT]
  PN2222A = NPN-Transistor [package="TO92 [THT]"]
  PN2222A_2 = NPN-Transistor [package="TO92 [THT]"]
  JP2 = USB_MICROB_PLUG [package=micro-b-ra-th]

nets:
  GND: BUTTON1.no_name_yet#1, BUTTON2.no_name_yet#1, Part1.GND, WS2812_LED_STRIP.GND, PN2222A.C, PN2222A_2.C, JP2.GND
  N1: BUTTON1.no_name_yet#2, Adafruit_Circuit_Playground_Express.D3_SCL, R2.Pin_1
  N2: BUTTON2.no_name_yet#2, Adafruit_Circuit_Playground_Express.D9, R1.Pin_1
  N3: LED1.cathode, PN2222A_2.E
  +5V: LED1.anode, LED2.anode, WS2812_LED_STRIP.+5V, U1.P, R1.Pin_0, R2.Pin_0, JP2.VCC
  N4: LED2.cathode, PN2222A.E
  N5: Part1.VBUS, U1.O
  N6: Adafruit_Circuit_Playground_Express.D6, WS2812_LED_STRIP.DI
  N7: Adafruit_Circuit_Playground_Express.D10, PN2222A_2.B
  N8: Adafruit_Circuit_Playground_Express.D2_SDA, PN2222A.B

custom parts:
  Arcade Button (red): Adafruit Arcade Button (red)
  Arcade Button (green): Adafruit Arcade Button (green)
  Adafruit Micro USB Breakout: Simple but effective - this breakout board has a USB Micro-B connector, with all 5 pins broken out. Great for pairing with a microcontroller with USB support, or adding USB 5V power to a project. We use a micro-AB connector with through-hole shielding pads for an excellent strong connection - it won't rip off by accident! Comes with one fully assembled and tested micro B breakout PCB and a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
  Adafruit Circuit Playground Dev Edition: Would you like to learn electronics, with an all-in-one board that has sensors and LEDs built in? Circuit Playground is here - and it's the best way to practice programming on real hardware with no soldering or sewing required! Circuit Playground features an ATmega32u4 processor, just like our popular Flora. The board's also round and has alligator-clip pads around it so you don't have to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
  Neopixel Strip -- Black (60/m): Neopixel Strip, Black, 60 pixels per meter.
